# Fritzing sketch Arduino-Pi-Serial-Connection-VD (saved by Fritzing 0.9.3b)
breadboards: 1

parts:
  MCU1 = Raspberry Pi Zero
  Part2 = Arduino Uno (Rev3)
  R1 = Resistor [tolerance=±5% resistance=3.3k package=THT]
  R2 = Resistor [tolerance=±5% resistance=2.2k package=THT]

nets:
  N1: MCU1.pin_2, MCU1.pin_4, Part2.5V
  N2: MCU1.pin_6, Part2.GND, R1.Pin_0
  N3: MCU1.pin_8, Part2.D4
  N4: MCU1.pin_10, R1.Pin_1, R2.Pin_0
  N5: Part2.D5_PWM, R2.Pin_1

notes:
  3K3
  2K2
