# Fritzing sketch Arduino-Pi-Serial-Connection (saved by Fritzing 0.9.3b)

parts:
  Part1 = Logic Level Converter
  MCU1 = Raspberry Pi Zero
  Part2 = Arduino Uno (Rev3)

nets:
  GND: Part1.GND, Part1.TX_LV, MCU1.pin_5, MCU1.pin_6, MCU1.pin_9, MCU1.pin_10, Part2.GND
  N1: Part1.LV, MCU1.pin_1
  N2: Part1.RX_LV, MCU1.pin_7, MCU1.pin_8
  N3: Part1.TX_HV, Part2.D5_PWM
  N4: Part1.RX_HV, Part2.D4
  N5: Part1.HV, MCU1.pin_2, MCU1.pin_4, Part2.5V
